# Fritzing sketch Project-AEC (saved by Fritzing 0.9.3b)
stripboards: 1

parts:
  Q1 = PNP-Transistor [package="TO92 [THT]"]
  C1 = Capacitor [package=cap-pth-small2]
  U1 = Voltage Regulator - 3.3V [package="TO220 [THT]"]
  C2 = Capacitor [package=cap-pth-small2]
  U2 = OP482 - Low Power, High Speed JFET Quad Operational Amplifier [part_number=OP482]
  R81_-_9k1_Resisitor = Resistor [tolerance=±5% resistance=9k package="2512 [SMD]"]
  R82_-_1k_Resistor = Resistor [tolerance=±10% resistance=1k package=THT]
  R89_-_20k_Resisitor = Resistor [tolerance=±5% resistance=9k package="2512 [SMD]"]
  R88_-_30k_Resistor = Resistor [tolerance=±10% resistance=1k package=THT]
  R86_-_30k_Resisitor = Resistor [tolerance=±5% resistance=9k package="2512 [SMD]"]
  R87_-_20k_Resistor1 = Resistor [tolerance=±10% resistance=1k package=THT]
  Red_LED = LEDs [package=led10mm]
  R83_-_1k_Resisitor = Resistor [tolerance=±5% resistance=9k package="2512 [SMD]"]
  D48_-_Green_LED = LEDs [package=led10mm]  # not connected
  R84_-_1k_Resisitor1 = Resistor [tolerance=±5% resistance=9k package="2512 [SMD]"]
  D47_-_Orange_LED = LEDs [package=led10mm]
  R85_-_1k_Resisitor = Resistor [tolerance=±5% resistance=9k package="2512 [SMD]"]
  Q2 = NPN-Transistor [package="TO92 [THT]"]
  R90_-_6k8_Resisitor = Resistor [tolerance=±5% resistance=9k package="2512 [SMD]"]
  D47_-_Orange_LED1 = LEDs [package=led10mm]
  R80_-_250_Resisitor = Resistor [tolerance=±5% resistance=9k package="2512 [SMD]"]
  D1 = Diode [package=diode-hv]
  LM331_V_-_Freq_converter = AD654 - Low Cost Monolithic Voltage-to-Frequency Converter [part_number=AD654]
  C17_-_100n = Capacitor [package=cap-pth-small2]
  R92_-_51k_Resisitor = Resistor [tolerance=±5% resistance=9k package="2512 [SMD]"]
  R91_-_100k_Resisitor_-_out_to_TEMP_VOLT = Resistor [tolerance=±5% resistance=9k package="2512 [SMD]"]
  C16_-_100n_-_out_to_GND_below = Capacitor [package=cap-pth-small2]
  R95_-_7k5_Resisitor_-_out_to_POT = Resistor [tolerance=±5% resistance=9k package="2512 [SMD]"]
  C18_-_1uF_Mylar_-_out_to_R96 = Electrolytic Capacitor [capacitance=100µF package="200 mil [THT, electrolytic]"]
  R94_-_100k_Resisitor_-_out_to_R96 = Resistor [tolerance=±5% resistance=9k package="2512 [SMD]"]
  R96_-_47_Resisitor_-_out_to_GND = Resistor [tolerance=±5% resistance=9k package="2512 [SMD]"]
  5V_into_R93_-_10k_Resisitor_-_out_PIN3/FreqOut = Resistor [tolerance=±5% resistance=9k package="2512 [SMD]"]
  U3 = POT [package=3362u]

nets:
  N1: Q1.E, Q1.B, Q1.C, C1.1, C1.2, U1.input_voltage, U1.GND, U1.output_voltage, C2.1, C2.2, U2.OUTA, U2.-INA, U2.+INA, U2.V+, U2.+INB, U2.+INC, U2.V-, U2.+IND, U2.-IND, U2.OUTD, R81_-_9k1_Resisitor.Pin_0, R81_-_9k1_Resisitor.Pin_1, R82_-_1k_Resistor.Pin_0, R82_-_1k_Resistor.Pin_1, R89_-_20k_Resisitor.Pin_0, R88_-_30k_Resistor.Pin_1, R86_-_30k_Resisitor.Pin_0, R87_-_20k_Resistor1.Pin_1, R83_-_1k_Resisitor.Pin_1, R84_-_1k_Resisitor1.Pin_0, R84_-_1k_Resisitor1.Pin_1, Q2.E, D47_-_Orange_LED1.C, R80_-_250_Resisitor.Pin_0, D1.A, LM331_V_-_Freq_converter.10V, LM331_V_-_Freq_converter.2p5V, LM331_V_-_Freq_converter.COMMON, LM331_V_-_Freq_converter.STROBE, LM331_V_-_Freq_converter.VBG, LM331_V_-_Freq_converter.V+, C17_-_100n.1, C17_-_100n.2, R92_-_51k_Resisitor.Pin_0, R92_-_51k_Resisitor.Pin_1, R91_-_100k_Resisitor_-_out_to_TEMP_VOLT.Pin_1, C16_-_100n_-_out_to_GND_below.2, R95_-_7k5_Resisitor_-_out_to_POT.Pin_0, C18_-_1uF_Mylar_-_out_to_R96.-, R94_-_100k_Resisitor_-_out_to_R96.Pin_0, R96_-_47_Resisitor_-_out_to_GND.Pin_0, 5V_into_R93_-_10k_Resisitor_-_out_PIN3/FreqOut.Pin_0, 5V_into_R93_-_10k_Resisitor_-_out_PIN3/FreqOut.Pin_1, U3.E, U3.S, U3.A
  N2: U2.-INB, U2.-INC, R89_-_20k_Resisitor.Pin_1, R88_-_30k_Resistor.Pin_0, R86_-_30k_Resisitor.Pin_1, R87_-_20k_Resistor1.Pin_0, R80_-_250_Resisitor.Pin_1, D1.C
  N3: U2.OUTB, U2.OUTC, Red_LED.A, D47_-_Orange_LED.C, R85_-_1k_Resisitor.Pin_0, R90_-_6k8_Resisitor.Pin_1
  N4: Red_LED.C, R83_-_1k_Resisitor.Pin_0
  N5: D47_-_Orange_LED.A, R85_-_1k_Resisitor.Pin_1
  N6: Q2.B, D47_-_Orange_LED1.A
  N7: Q2.C, R90_-_6k8_Resisitor.Pin_0
  N8: LM331_V_-_Freq_converter.5V, LM331_V_-_Freq_converter.CAP, R91_-_100k_Resisitor_-_out_to_TEMP_VOLT.Pin_0, C16_-_100n_-_out_to_GND_below.1, R95_-_7k5_Resisitor_-_out_to_POT.Pin_1
  N9: C18_-_1uF_Mylar_-_out_to_R96.+, R94_-_100k_Resisitor_-_out_to_R96.Pin_1, R96_-_47_Resisitor_-_out_to_GND.Pin_1
